// Logisim project 4x1_Multiplexer_NOR.circ as structural Verilog: 1 circuit, main circuit main
module main (
  input  I0,
  input  I1,
  input  I2,
  input  I3,
  input  S0,
  input  S1,
  output Y
);

  wire G1_out, G2_out, G3_out, G4_out, G5_out, G6_out, G7_out, G8_out, G9_out, G10_out, G11_out, G12_out,
       G13_out, G14_out, G15_out, G16_out;

  nor G2 (G2_out, S0, S0);
  nor G1 (G1_out, S1, S1);
  nor G3 (G3_out, G1_out, G2_out);
  nor G6 (G6_out, G1_out, S0);
  nor G9 (G9_out, S1, G2_out);
  nor G12 (G12_out, S1, S0);
  nor G4 (G4_out, G3_out, I0);
  nor G7 (G7_out, G6_out, I1);
  nor G10 (G10_out, G9_out, I2);
  nor G13 (G13_out, G12_out, I3);
  nor G5 (G5_out, G4_out, G4_out);
  nor G8 (G8_out, G7_out, G7_out);
  nor G11 (G11_out, G10_out, G10_out);
  nor G14 (G14_out, G13_out, G13_out);
  nor G15 (G15_out, G5_out, G8_out);
  nor G16 (G16_out, G11_out, G14_out);
  nor G17 (Y, G15_out, G16_out);
endmodule
